// Logisim project Assignment.circ as structural Verilog: 1 circuit, main circuit main
module main (
  input  S
);

  wire buffer_1_out;

  buf buffer_1 (buffer_1_out, S);
  LED L (.in(buffer_1_out));
endmodule
