// Logisim project Assignment2.circ as structural Verilog: 1 circuit, main circuit main
module main (
  input  A0,
  input  A1,
  input  S0,
  input  S1,
  input  R0,
  input  R1,
  output GRANT,
  output Unlock_Room0,
  output Unlock_Room1,
  output Unlock_Room2,
  output Unlock_Room3
);

  wire R0_prime_out, R1_prime_out, xnor_1_out, xnor_2_out;

  xnor xnor_1 (xnor_1_out, A0, S0);
  xnor xnor_2 (xnor_2_out, A1, S1);
  not R0_prime (R0_prime_out, R0);
  not R1_prime (R1_prime_out, R1);
  and and_1 (GRANT, xnor_1_out, xnor_2_out);
  and and_2 (Unlock_Room0, R1_prime_out, R0_prime_out, GRANT);
  and and_3 (Unlock_Room1, R1_prime_out, R0, GRANT);
  and and_4 (Unlock_Room2, R1, R0_prime_out, GRANT);
  and and_5 (Unlock_Room3, R1, R0, GRANT);
endmodule
