// Logisim project DiscussionAssignment.circ as structural Verilog: 1 circuit, main circuit main
module main (
  input  A0,
  input  B0,
  input  in_3,
  output S0,
  output C0
);

  xor xor_1 (S0, A0, B0);
  and and_1 (C0, A0, B0);
endmodule
