// Logisim project adder.circ as structural Verilog: 1 circuit, main circuit main
module main (
  input  A0,
  input  B0,
  input  A1,
  input  B1,
  output S0,
  output C0,
  output S1,
  output Cout
);

  wire G1_out, G2_out, X1_out;

  xor xor_1 (S0, A0, B0);
  and and_1 (C0, A0, B0);
  xor X1 (X1_out, A1, B1);
  and G1 (G1_out, A1, B1);
  xor xor_2 (S1, X1_out, C0);
  and G2 (G2_out, C0, X1_out);
  or or_1 (Cout, G1_out, G2_out);
endmodule
