// Logisim project scoreboard.circ as structural Verilog: 1 circuit, main circuit main
module main (
);

  wire LATCH_out, RESET_out, SCORE_out;
  wire [3:0] counter_1_q, register_1_q;

  Button SCORE (.out(SCORE_out));
  Counter #(.width(4), .max('hf)) counter_1 (
    .Q(counter_1_q), .clk(SCORE_out), .clr(RESET_out));  // open: load, D, count, carry
  Button RESET (.out(RESET_out));
  Button LATCH (.out(LATCH_out));
  Register #(.width(4)) register_1 (.D(counter_1_q), .Q(register_1_q), .clk(LATCH_out), .clr(RESET_out));  // open: en
  Hex_Digit_Display hex_digit_display_1 (.value(register_1_q));  // open: dp
endmodule
