// Logisim project Unit4_Calculator_Reference.circ as structural Verilog: 3 circuits, main circuit main
module main (
  input  [3:0] A__4_bit,
  input  [3:0] B__4_bit,
  input  [1:0] OP__2_bit_opcode,
  output [7:0] Result__8_bit,
  output Z__result_is_zero,
  output V__overflow__ADD_SUB_only,
  output DIV0__divide_by_zero
);

  wire comparator_1_eq, not_1_out, OP_bit_0, OP_bit_1, V_from_adder;
  wire [3:0] AddSub4_s__result;
  wire [7:0] ADD_SUB_result, DIV_result, MUL_result, undriven, undriven_2;

  AddSub4 AddSub4 (
    .A(A__4_bit), .B(B__4_bit), .SUB(OP_bit_0), .S__result(AddSub4_s__result), .V__overflow(V_from_adder));  // open: C__carry_out
  Multiplier #(.width(4)) multiplier_1 (
    .a(A__4_bit), .b(B__4_bit), .out(MUL_result[3:0]), .cout(MUL_result[7:4]));  // open: cin
  Divider #(.width(4)) divider_1 (
    .a(A__4_bit), .b(B__4_bit), .out(DIV_result[3:0]), .rem(DIV_result[7:4]));  // open: upper
  assign ADD_SUB_result = {{4{AddSub4_s__result[3]}}, AddSub4_s__result};  // Bit_Extender bit_extender_1
  Multiplexer #(.select(2), .width(8)) multiplexer_1 (
    .in0(ADD_SUB_result), .in1(ADD_SUB_result), .in2(MUL_result), .in3(DIV_result), .out(Result__8_bit),
    .sel(OP__2_bit_opcode));  // open: en
  Comparator #(.width(4), .mode("unsigned")) comparator_1 (
    .a(B__4_bit), .b(4'b0000), .eq(comparator_1_eq));  // open: gt, lt
  not not_1 (not_1_out, OP_bit_1);
  Hex_Digit_Display hex_digit_display_1 (.value(undriven_2[7:4]));  // open: dp
  Comparator #(.width(8), .mode("unsigned")) comparator_2 (
    .a(undriven), .b({8{1'b0}}), .eq(Z__result_is_zero));  // open: gt, lt
  and and_1 (V__overflow__ADD_SUB_only, V_from_adder, not_1_out);
  and and_2 (DIV0__divide_by_zero, OP_bit_1, comparator_1_eq, OP_bit_0);
  Hex_Digit_Display hex_digit_display_2 (.value(undriven_2[3:0]));  // open: dp

  // Other names for the same wires on the sheet: A[3:0] = A__4_bit; B[3:0] = B__4_bit; OP[1:0] = OP__2_bit_opcode

  // Notes on the sheet:
  //   (OP bit 0 drives SUB)
  //   4-bit Binary Calculator      OP:  00 = ADD   01 = SUB   10 = MUL   11 = DIV
  //   Adder / Subtractor (4 full adders)
  //   Multiplier (A x B, 8-bit product)
  //   Divider (high digit = remainder, low = quotient)
  //   00 ADD
  //   01 SUB
  //   10 MUL
  //   11 DIV
  //   B = 0 ?
  //   Operation select (MUX)
  //   Result = 0 ?
  //   Result in hex
endmodule

module AddSub4 (
  input  [3:0] A,
  input  [3:0] B,
  input  SUB,
  output [3:0] S__result,
  output C__carry_out,
  output V__overflow
);

  wire bx0, bx1, bx2, bx3, c1, c2, c3;

  xor xor_1 (bx0, B[0], SUB);
  xor xor_2 (bx1, B[1], SUB);
  xor xor_3 (bx2, B[2], SUB);
  xor xor_4 (bx3, B[3], SUB);
  FullAdder fulladder_1 (.A(A[0]), .B(bx0), .Cin(SUB), .S__sum(S__result[0]), .Cout__carry_out(c1));
  FullAdder fulladder_2 (.A(A[1]), .B(bx1), .Cin(c1), .S__sum(S__result[1]), .Cout__carry_out(c2));
  FullAdder fulladder_3 (.A(A[2]), .B(bx2), .Cin(c2), .S__sum(S__result[2]), .Cout__carry_out(c3));
  FullAdder fulladder_4 (.A(A[3]), .B(bx3), .Cin(c3), .S__sum(S__result[3]), .Cout__carry_out(C__carry_out));
  xor xor_5 (V__overflow, c3, C__carry_out);

  // Other names for the same wires on the sheet: c0 = SUB; c4 = C__carry_out; s0 = S__result[0]; s1 = S__result[1];
  //   s2 = S__result[2]; s3 = S__result[3]

  // Notes on the sheet:
  //   Split A and B into bits (bit 0 = top)
  //   SUB also feeds carry-in c0 (the +1)
  //   XOR row: flips B when SUB = 1
  //   4-bit Adder / Subtractor:  SUB = 0 adds,  SUB = 1 subtracts (A + NOT B + 1)
  //   4 full adders (ripple carry)
  //   Join sum bits, flags
endmodule

module FullAdder (
  input  A,
  input  B,
  input  Cin,
  output S__sum,
  output Cout__carry_out
);

  wire and_1_out, and_2_out, undriven, undriven_2, undriven_3, xor_1_out;

  xor xor_1 (xor_1_out, A, B);
  and and_1 (and_1_out, undriven, B);
  xor xor_2 (S__sum, xor_1_out, Cin);
  and and_2 (and_2_out, undriven_2, undriven_3);
  or or_1 (Cout__carry_out, and_1_out, and_2_out);

  // Notes on the sheet:
  //   Full Adder:  S = A XOR B XOR Cin,   Cout = A.B + Cin.(A XOR B)
endmodule
