// Logisim project Unit5_Combination_Lock.circ as structural Verilog: 1 circuit, main circuit main
module main (
  input  [3:0] DIGIT__0_9,
  output UNLOCKED,
  output ALARM,
  output [1:0] STATE,
  output [1:0] TRIES
);

  wire ADMIN, CLEAR_STATE, CLEAR_TRIES, ENTER, LOCK, WRONG;
  wire [1:0] NEXT_STATE;
  wire [3:0] bit_extender_1_out, bit_extender_2_out;

  Button u_ENTER (.out(ENTER));
  Button u_LOCK (.out(LOCK));
  Button ADMIN_RESET (.out(ADMIN));
  Hex_Digit_Display hex_digit_display_1 (.value(DIGIT__0_9));  // open: dp
  Register #(.width(2)) u_STATE (.D(NEXT_STATE), .Q(STATE), .clk(ENTER), .clr(CLEAR_STATE));  // open: en
  Counter #(.width(2), .max('h3), .ongoal("stay")) u_TRIES (
    .count(WRONG), .Q(TRIES), .clk(ENTER), .clr(CLEAR_TRIES));  // open: load, D, carry
  ROM #(.addrWidth(7), .dataWidth(4)) LOCK_PLD (
    .addr({ALARM, STATE, DIGIT__0_9}), .data({WRONG, UNLOCKED, NEXT_STATE}));  // open: sel
  or or_1 (CLEAR_STATE, LOCK, ADMIN);
  or or_2 (CLEAR_TRIES, ADMIN, UNLOCKED);
  Comparator #(.width(2), .mode("unsigned")) comparator_1 (.a(TRIES), .b(2'b11), .eq(ALARM));  // open: gt, lt
  Hex_Digit_Display hex_digit_display_2 (.value(bit_extender_1_out));  // open: dp
  assign bit_extender_1_out = {{2{1'b0}}, STATE};  // Bit_Extender bit_extender_1
  LED DOOR_OPEN (.in(UNLOCKED));
  LED u_ALARM (.in(ALARM));
  Hex_Digit_Display hex_digit_display_3 (.value(bit_extender_2_out));  // open: dp
  assign bit_extender_2_out = {{2{1'b0}}, TRIES};  // Bit_Extender bit_extender_2

  // Other names for the same wires on the sheet: DIGIT[3:0] = DIGIT__0_9; UNLOCK = UNLOCKED

  // Notes on the sheet:
  //   Keypad and buttons
  //   Digit entered
  //   State register (2 D flip-flops)
  //   Failed-attempt counter (stops at 3)
  //   Digital Combination Lock  (code 7 - 3 - 9)   PLD: 128 x 4 PROM
  //   PLD: PROM programmed with the lock's truth table
  //   address = ALARM, STATE, DIGIT     data = WRONG, UNLOCK, NEXT STATE
  //   contents of LOCK_PLD (hex, n*v repeats v):
  //   8 8 8 8 8 8 8 1 8 8 8 8 8 8 8 8 8 8 8 2 8 8 8 8 8 8 8 8 8 8 8 8 8 8 8 8 8 8 8 8 8 3 8 8 8 8 8 8 7 7
  //   7 7 7 7 7 7 7 7 7 7 7 7 7 7 0 0 0 0 0 0 0 0 0 0 0 0 0 0 0 0 0 0 0 0 0 0 0 0 0 0 0 0 0 0 0 0 0 0 0 0
  //   0 0 0 0 0 0 0 0 0 0 0 0 0 0 0 0 0 0 0 0 0 0 0 0 0 0 0 0
  //   Reset logic
  //   Alarm after 3 wrong digits
  //   Progress
  //   Lock outputs
  //   Wrong tries
endmodule
