// Logisim project bus_conflict.circ as structural Verilog: 1 circuit, main circuit main
module main (
  input  A,
  input  B,
  output BUS
);


  assign B = A;
  assign BUS = A;

  // Notes on the sheet:
  //   Symbol resolution in hardware: two drivers, one label
endmodule
